# Fritzing sketch Ai RoverTank (saved by Fritzing 0.9.2b)
breadboards: 3

parts:
  Part1 = Arduino Uno (Rev3) - ICSP
  RF1 = nRF8001 Bluetooth LE Breakout
  IMU1 = Adafruit 10-DOF IMU Breakout  # not connected
  J1 = Basic Servo
  PING)))_SENSOR1 = PING))) SENSOR
  LED1 = LEDs [package=led10mm]
  R1 = Resistor [tolerance=±5% resistance=220 package=THT]

nets:
  N1: Part1.ICSP_MISO, Part1.D12/MISO, RF1.MISO
  N2: Part1.ICSP_MOSI, Part1.D11_PWM/MOSI, RF1.MOSI
  N3: Part1.D8, LED1.C
  N4: Part1.D9_PWM, RF1.RST
  N5: Part1.D10_PWM/SS, RF1.REQ
  N6: Part1.D13/SCK, RF1.SCK
  N7: Part1.D5_PWM, J1.pulse
  5V: Part1.D6_PWM, Part1.5V, RF1.VIN, PING)))_SENSOR1.5V, PING)))_SENSOR1.SIGNAL
  GND: Part1.GND, RF1.GND, J1.gnd, PING)))_SENSOR1.GND, R1.Pin_0
  N8: LED1.A, R1.Pin_1

notes:
  -Green is right Motor - black is GND
  -Blue is left motor - brown is GND
  Servo Turns Ping Sensor

custom parts:
  nRF8001 Bluetooth LE Breakout: nRF8001 Breakout Board

// code stored in the sketch: roverTank.ino
#include <SPI.h>
#include <Servo.h>
#include <Wire.h>

#include "Adafruit_BLE_UART.h"
#include <Adafruit_Sensor.h>
#include <Adafruit_LSM303_U.h>
#include <Adafruit_L3GD20_U.h>
#include <Adafruit_BMP085_U.h>
#include <Adafruit_10DOF.h>

#define ADAFRUITBLE_REQ 10
#define ADAFRUITBLE_RDY 2
#define ADAFRUITBLE_RST 9

#define RIGHTMOTOR 4
#define LEFTMOTOR 7
#define PINGSENSOR 6
#define BLUELED 8
#define PINGSERVO 5

#define CENTER 85
#define LEFT 1
#define RIGHT 167

Adafruit_10DOF                dof   = Adafruit_10DOF();
Adafruit_LSM303_Accel_Unified accel = Adafruit_LSM303_Accel_Unified(30301);
Adafruit_LSM303_Mag_Unified   mag   = Adafruit_LSM303_Mag_Unified(30302);

Servo ps;
Servo rm;
Servo lm;

aci_evt_opcode_t status;
aci_evt_opcode_t laststatus = ACI_EVT_DISCONNECTED;
int myBytes[2];
unsigned long interval = 3000;
unsigned long currentMillis = millis();
unsigned long previousMillis;
boolean AIMode = false;

Adafruit_BLE_UART BTLEserial = Adafruit_BLE_UART(ADAFRUITBLE_REQ, ADAFRUITBLE_RDY, ADAFRUITBLE_RST);

void setup(void) {
    Serial.begin(9600);
    while(!Serial);
    Serial.println(F("Adafruit Bluefruit Low Energy nRF8001 Print echo demo"));

    mag.begin();
    BTLEserial.begin();
    pinMode(BLUELED, OUTPUT);

    rm.attach(RIGHTMOTOR);
    lm.attach(LEFTMOTOR);
    ps.attach(PINGSERVO);
    ps.write(CENTER);
    delay(3000);
    Serial.print("Done with Setup");
}

void loop() {
    /*setMotorSpeed(1700, 1300);               //values go from 215 - 280 ish in chasie*/
    /*Serial.println(getCurrentHeading());     //values go from 0 - 359 outside of chasie*/
    currentMillis = millis();
    long distance = getPingSensorDistance();
    if (distance < 30) {
        digitalWrite(BLUELED, HIGH);
        while(getPingSensorDistance() < 40) {
            setMotorSpeed(1600, 1600);
            delay(30);
        }
        setMotorSpeed(1500, 1500);
        if (AIMode) findNextDirection();
    } else {
        if (AIMode) setMotorSpeed(1400, 1400);
        digitalWrite(BLUELED, LOW);
    }
    checkBTStatus();
    if (status == ACI_EVT_CONNECTED) {
        if (!AIMode) {
        handlingBT();
        } else {
        if (BTLEserial.available()){
            for (int x = 0; x < 2; x++) {
                myBytes[x] = BTLEserial.read();
                if (myBytes[x] != 0x96) AIMode = false;
                previousMillis = currentMillis;
            }

        }
    }
  }
  /*delay(200);*/
}
void findNextDirection() {
    long right = getRightDistance();
    Serial.print("Right: ");Serial.println(right);
    delay(500);
    long left = getLeftDistance();
    Serial.print("Left: ");Serial.println(left);
    if ((left > 30) || (right > 30)) {
        if (left > right) {
            turnLeft(getCurrentHeading());
        } else if (right > left) {
            turnRight(getCurrentHeading());
        } else {
            while(getPingSensorDistance() < 50) {
                setMotorSpeed(1600, 1600);
                delay(30);
            }
        }
    } else {
        while(getPingSensorDistance() < 50) {
            setMotorSpeed(1600, 1600);
            delay(30);
        }
    }
}
long getRightDistance() {
    ps.write(RIGHT);
    delay(300);
    long distanceR = getPingSensorDistance();
    delay(150);
    ps.write(CENTER);
    return distanceR;
}

long getLeftDistance() {
    ps.write(LEFT);
    delay(300);
    long distanceL = getPingSensorDistance();
    delay(150);
    ps.write(CENTER);
    return distanceL;
}

long getPingSensorDistance() {
    pinMode(PINGSENSOR, OUTPUT);
    digitalWrite(PINGSENSOR, LOW);
    delayMicroseconds(2);
    digitalWrite(PINGSENSOR, HIGH);
    delayMicroseconds(5);
    pinMode(PINGSENSOR, INPUT);
    long duration = pulseIn(PINGSENSOR,HIGH);
    return duration / 29 / 2;
}

int getCurrentHeading() {
    sensors_event_t event;
    sensors_vec_t   orientation;
    mag.getEvent(&event);
    if (dof.magGetOrientation(SENSOR_AXIS_Z, &event, &orientation)) {
      return orientation.heading;
    }
    return -1;
}
int getLeftHeading(int heading) {  //subtract 90
    int newHeading = heading - 90;
    while (newHeading < 0) {
        newHeading = newHeading + 360;
    }
    return newHeading;

}
int getRightHeading(int heading) { //add 90
    int newHeading = heading + 90;
    while (newHeading >= 360) {
        newHeading = newHeading - 360;
    }
    return newHeading;
}

void handlingBT() {
    if(currentMillis - previousMillis> interval) {
        previousMillis = currentMillis;
        interval = 3000;
        for (int x = 0; x < 2; x++) {
            myBytes[x] = 0x96;
        }
    }
    if (BTLEserial.available() == 2) {
        for (int x = 0; x < 2; x++) {
            myBytes[x] = BTLEserial.read();
            previousMillis = currentMillis;
        }
        setMotorSpeed(myBytes[0] * 10, myBytes[1] * 10);
    }
}
void setMotorSpeed(int left, int right) {
    lm.writeMicroseconds(left);
    rm.writeMicroseconds(right);
}
void turnLeft(int heading) {
    while((getCurrentHeading() > getLeftHeading(heading))){
        Serial.print("TURNINGHeading: ");Serial.println(getCurrentHeading());
        Serial.print("TurnLeftHeading: ");Serial.println(getLeftHeading(heading));
        if (getCurrentHeading() < getLeftHeading(heading) + 20) {
            Serial.println("TURNEDTOOO MUCHHHHHH");
        }
        setMotorSpeed(1700, 1300);
        /*delay(200);*/
    }
    setMotorSpeed(1500, 1500);
}
void turnRight(int heading) {
    while((getCurrentHeading() < getRightHeading(heading))){
        Serial.print("TURNINGHeading: ");Serial.println(getCurrentHeading());
        Serial.print("TurnRightHeading: ");Serial.println(getRightHeading(heading));
        setMotorSpeed(1300, 1700);
        /*delay(200);*/
    }
    setMotorSpeed(1500, 1500);
}
void reverseFor(int time) {
    setMotorSpeed(1700, 1700);
    delay(time);
    setMotorSpeed(1500, 1500);
}
void checkBTStatus() {
    BTLEserial.pollACI();
    status = BTLEserial.getState();
    if (status != laststatus) {
    if (status == ACI_EVT_CONNECTED) {
      previousMillis = currentMillis;
    }
    if (status == ACI_EVT_DISCONNECTED) {
      setMotorSpeed(1500, 1500);
    }
    laststatus = status;
    }
}
