# Fritzing sketch Bluetooth RoverTank (saved by Fritzing 0.9.2b)
breadboards: 1

parts:
  Part1 = Arduino Uno (Rev3) - ICSP
  RF1 = nRF8001 Bluetooth LE Breakout
  IC1 = H-Bridge [package=THT]
  M1 = DC Motor
  VCC1 = Battery
  M2 = DC Motor

nets:
  N1: Part1.ICSP_MISO, Part1.D12/MISO, RF1.MISO
  N2: Part1.ICSP_MOSI, Part1.D11_PWM/MOSI, RF1.MOSI
  N3: Part1.D8, IC1.4A
  N4: Part1.D9_PWM, RF1.RST
  N5: Part1.D10_PWM/SS, RF1.REQ
  N6: Part1.D13/SCK, RF1.SCK
  N7: Part1.D2, RF1.RDY
  N8: Part1.D3_PWM, IC1.1A
  N9: Part1.D4, IC1.2A
  N10: Part1.D5_PWM, IC1.1_2EN
  N11: Part1.D6_PWM, IC1.3_4EN
  N12: Part1.D7, IC1.3A
  5V: Part1.5V, RF1.VIN, IC1.VCC1
  GND: Part1.GND, RF1.GND, IC1.GND1, IC1.GND2, IC1.GND3, IC1.GND4, VCC1.-
  N13: IC1.1Y, M1.pin_1
  N14: IC1.2Y, M1.pin_2
  N15: IC1.VCC2, VCC1.+
  N16: IC1.3Y, M2.pin_2
  N17: IC1.4Y, M2.pin_1

custom parts:
  nRF8001 Bluetooth LE Breakout: nRF8001 Breakout Board
