# Fritzing sketch RoverTank (saved by Fritzing 0.9.0b)
breadboards: 1

parts:
  Part1 = Arduino Uno (Rev3)
  S1 = Pushbutton [package="[THT]"]
  S2 = Pushbutton [package="[THT]"]
  M1 = DC Motor
  M2 = DC Motor
  U1 = POT [package=pot_mammoth]
  R1 = Rotary Potentiometer (Large) [maximum_resistance=100kΩ package=THT]
  S3 = Pushbutton [package="[THT]"]
  S4 = Pushbutton [package="[THT]"]
  R2 = Resistor [tolerance=±5% resistance=10k package=THT]
  R3 = Resistor [tolerance=±5% resistance=10k package=THT]
  R4 = Resistor [tolerance=±5% resistance=10k package=THT]
  R5 = Resistor [tolerance=±5% resistance=10k package=THT]
  IC1 = H-Bridge [package=THT]
  VCC1 = Battery

nets:
  N1: Part1.A0, U1.A
  N2: Part1.A1, R1.wiper
  N3: Part1.D8, IC1.2A
  N4: Part1.D9_PWM, IC1.1_2EN
  N5: Part1.D10_PWM/SS, S2.Pin_1, S2.Pin_2
  N6: Part1.D11_PWM/MOSI, S1.Pin_1, S1.Pin_2
  N7: Part1.D2, IC1.3A
  N8: Part1.D3_PWM, IC1.3_4EN
  N9: Part1.D4, IC1.4A
  N10: Part1.D5_PWM, S4.Pin_1, S4.Pin_2
  N11: Part1.D6_PWM, S3.Pin_1, S3.Pin_2
  N12: Part1.D7, IC1.1A
  N13: Part1.5V, S1.Pin_3, S1.Pin_4, S2.Pin_3, S2.Pin_4, U1.E, R1.leg2, S3.Pin_3, S3.Pin_4, S4.Pin_3, S4.Pin_4, R2.Pin_0, R3.Pin_0, R4.Pin_0, R5.Pin_0, IC1.VCC1
  GND: Part1.GND, U1.S, R1.leg1, R2.Pin_1, R3.Pin_1, R4.Pin_1, R5.Pin_1, IC1.GND1, IC1.GND2, IC1.GND3, IC1.GND4, VCC1.-
  N14: M1.pin_1, IC1.1Y
  N15: M1.pin_2, IC1.2Y
  N16: M2.pin_1, IC1.4Y
  N17: M2.pin_2, IC1.3Y
  N18: IC1.VCC2, VCC1.+

notes:
  pink is M1
  cyan is M2
